// Logisim project AsteroidPong.circ as structural Verilog: 9 circuits, main circuit main
module main (
  input  in_1,
  input  in_2,
  output out_3
);

  wire _128_HZ_out, reductordefrecuencia_1_clock_salida;
  wire [6:0] keyboard_1_data;
  wire [31:0] worldprocess_1_p3, worldprocess_1_p4, worldprocess_1_p5, worldprocess_1_p6, worldprocess_1_p7,
       worldprocess_1_p8, worldprocess_1_p9, worldprocess_1_p10, worldprocess_1_p11, worldprocess_1_p12,
       worldprocess_1_p13, worldprocess_1_p14, worldprocess_1_p15, worldprocess_1_p16, worldprocess_1_p17,
       worldprocess_1_p18, worldprocess_1_p19, worldprocess_1_p20, worldprocess_1_p21, worldprocess_1_p22,
       worldprocess_1_p23, worldprocess_1_p24, worldprocess_1_p25, worldprocess_1_p26, worldprocess_1_p27,
       worldprocess_1_p28, worldprocess_1_p29, worldprocess_1_p30, worldprocess_1_p31, worldprocess_1_p32,
       worldprocess_1_p33, worldprocess_1_p34;

  Clock _128_HZ (.out(_128_HZ_out));
  Keyboard keyboard_1 (.clk(_128_HZ_out), .re(in_1), .clr(in_2), .avail(out_3), .data(keyboard_1_data));
  ReductorDeFrecuencia reductordefrecuencia_1 (
    .Clock_Entrada(_128_HZ_out), .Clock_salida(reductordefrecuencia_1_clock_salida));
  // WorldProcess worldprocess_1: pin names not known; wires that end beside it: keyboard_1_data, reductordefrecuencia_1_clock_salida, worldprocess_1_p3, worldprocess_1_p4, worldprocess_1_p5, worldprocess_1_p6, worldprocess_1_p7, worldprocess_1_p8, worldprocess_1_p9, worldprocess_1_p10, worldprocess_1_p11, worldprocess_1_p12, worldprocess_1_p13, worldprocess_1_p14, worldprocess_1_p15, worldprocess_1_p16, worldprocess_1_p17, worldprocess_1_p18, worldprocess_1_p19, worldprocess_1_p20, worldprocess_1_p21, worldprocess_1_p22, worldprocess_1_p23, worldprocess_1_p24, worldprocess_1_p25, worldprocess_1_p26, worldprocess_1_p27, worldprocess_1_p28, worldprocess_1_p29, worldprocess_1_p30, worldprocess_1_p31, worldprocess_1_p32, worldprocess_1_p33, worldprocess_1_p34
  DotMatrix #(.inputtype("row"), .matrixcols(32), .matrixrows(32)) dotmatrix_1 (
    .row0(worldprocess_1_p3), .row1(worldprocess_1_p4), .row2(worldprocess_1_p5), .row3(worldprocess_1_p6),
    .row4(worldprocess_1_p7), .row5(worldprocess_1_p8), .row6(worldprocess_1_p9), .row7(worldprocess_1_p10),
    .row8(worldprocess_1_p11), .row9(worldprocess_1_p12), .row10(worldprocess_1_p13),
    .row11(worldprocess_1_p14), .row12(worldprocess_1_p15), .row13(worldprocess_1_p16),
    .row14(worldprocess_1_p17), .row15(worldprocess_1_p18), .row16(worldprocess_1_p19),
    .row17(worldprocess_1_p20), .row18(worldprocess_1_p21), .row19(worldprocess_1_p22),
    .row20(worldprocess_1_p23), .row21(worldprocess_1_p24), .row22(worldprocess_1_p25),
    .row23(worldprocess_1_p26), .row24(worldprocess_1_p27), .row25(worldprocess_1_p28),
    .row26(worldprocess_1_p29), .row27(worldprocess_1_p30), .row28(worldprocess_1_p31),
    .row29(worldprocess_1_p32), .row30(worldprocess_1_p33), .row31(worldprocess_1_p34));
endmodule

module Player (
  input  [6:0] in_1,
  output [31:0] out_2
);

  wire comparator_1_eq, comparator_2_eq, playermovselect_1_anterior, playermovselect_1_siguiente;
  wire [4:0] counter_1_q;

  Comparator #(.width(7), .mode("unsigned")) comparator_1 (
    .a(7'b1100001), .b(in_1), .eq(comparator_1_eq));  // open: gt, lt
  Comparator #(.width(7), .mode("unsigned")) comparator_2 (
    .a(7'b1100100), .b(in_1), .eq(comparator_2_eq));  // open: gt, lt
  PlayerMovSelect playermovselect_1 (
    .a(comparator_1_eq), .d(comparator_2_eq), .anterior(playermovselect_1_anterior),
    .siguiente(playermovselect_1_siguiente));
  PlayerMovement playermovement_1 (.in_1(counter_1_q), .out_2(out_2));
  Counter #(.width(5), .max('h1f)) counter_1 (
    .load(playermovselect_1_anterior), .Q(counter_1_q), .clk(playermovselect_1_siguiente));  // open: D, count, carry, clr
endmodule

module PlayerMovSelect (
  input  a,
  input  d,
  output anterior,
  output siguiente
);

  wire and_2_out, and_3_out, not_1_out, not_2_out, not_3_out;

  not not_1 (not_1_out, d);
  not not_2 (not_2_out, a);
  not not_3 (not_3_out, d);
  and and_1 (anterior, a, not_1_out);
  and and_2 (and_2_out, not_2_out, d);
  and and_3 (and_3_out, a, not_3_out);
  or or_1 (siguiente, and_2_out, and_3_out);
endmodule

// at
module RandomSystem (
  input  in_1,
  output [31:0] out_2
);

  wire [4:0] random_1_out;

  Random #(.width(5)) random_1 (.clk(in_1), .next(1'b1), .out(random_1_out));  // open: clr
  Decoder #(.select(5)) decoder_1 (
    .out0(out_2[31]), .out1(out_2[30]), .out2(out_2[29]), .out3(out_2[28]), .out4(out_2[27]),
    .out5(out_2[26]), .out6(out_2[25]), .out7(out_2[24]), .out8(out_2[23]), .out9(out_2[22]),
    .out10(out_2[21]), .out11(out_2[20]), .out12(out_2[19]), .out13(out_2[18]), .out14(out_2[17]),
    .out15(out_2[16]), .out16(out_2[15]), .out17(out_2[14]), .out18(out_2[13]), .out19(out_2[12]),
    .out20(out_2[11]), .out21(out_2[10]), .out22(out_2[9]), .out23(out_2[8]), .out24(out_2[7]),
    .out25(out_2[6]), .out26(out_2[5]), .out27(out_2[4]), .out28(out_2[3]), .out29(out_2[2]),
    .out30(out_2[1]), .out31(out_2[0]), .sel(random_1_out));  // open: en
endmodule

module PlayerMovement (
  input  [4:0] in_1,
  output [31:0] out_2
);

  Multiplexer #(.select(5), .width(32)) multiplexer_1 (
    .in0(32'he0000000), .in1(32'h70000000), .in2(32'h38000000), .in3(32'h1c000000), .in4(32'he000000),
    .in5(32'h7000000), .in6(32'h3800000), .in7(32'h1c00000), .in8(32'he00000), .in9(32'h700000),
    .in10(32'h380000), .in11(32'h1c0000), .in12(32'he0000), .in13(32'h70000), .in14(32'h38000),
    .in15(32'h1c000), .in16(32'he000), .in17(32'h7000), .in18(32'h3800), .in19(32'h1c00), .in20(32'he00),
    .in21(32'h700), .in22(32'h380), .in23(32'h1c0), .in24(32'he0), .in25(32'h70), .in26(32'h38),
    .in27(32'h1c), .in28(32'he), .in29(32'h7), .in30(32'h80000003), .in31(32'hc0000001), .out(out_2),
    .sel(in_1));  // open: en
endmodule

module WorldProcess (
  input  reloj,
  output [31:0] F0,
  output [31:0] F1,
  output [31:0] F2,
  output [31:0] F3,
  output [31:0] F4,
  output [31:0] F5,
  output [31:0] F6,
  output [31:0] F7,
  output [31:0] F8,
  output [31:0] F9,
  output [31:0] F10,
  output [31:0] F11,
  output [31:0] F12,
  output [31:0] F13,
  output [31:0] F14,
  output [31:0] F15,
  output [31:0] F16,
  output [31:0] F17,
  output [31:0] F18,
  output [31:0] F19,
  output [31:0] F20,
  output [31:0] F21,
  output [31:0] F22,
  output [31:0] F23,
  output [31:0] F24,
  output [31:0] F25,
  output [31:0] F26,
  output [31:0] F27,
  output [31:0] F28,
  output [31:0] F29,
  output [31:0] F30
);

  wire counter_1_carry;
  wire [4:0] counter_1_q;
  wire [31:0] randomsystem_1_out_2;

  Counter #(.width(5), .max('h1f)) counter_1 (
    .Q(counter_1_q), .carry(counter_1_carry), .clk(reloj));  // open: load, D, count, clr
  RandomSystem randomsystem_1 (.in_1(counter_1_carry), .out_2(randomsystem_1_out_2));
  Demultiplexer #(.select(5), .width(32)) demultiplexer_1 (
    .out0(F0), .out1(F1), .out2(F2), .out3(F3), .out4(F4), .out5(F5), .out6(F6), .out7(F7), .out8(F8),
    .out9(F9), .out10(F10), .out11(F11), .out12(F12), .out13(F13), .out14(F14), .out15(F15), .out16(F16),
    .out17(F17), .out18(F18), .out19(F19), .out20(F20), .out21(F21), .out22(F22), .out23(F23), .out24(F24),
    .out25(F25), .out26(F26), .out27(F27), .out28(F28), .out29(F29), .out30(F30), .in(randomsystem_1_out_2),
    .sel(counter_1_q));  // open: out31, en
endmodule

module ReductorDeFrecuencia (
  input  Clock_Entrada,
  output Clock_salida
);

  wire j_k_ff_1_q, j_k_ff_2_q;

  J_K_Flip_Flop j_k_ff_1 (.J(1'b1), .clk(Clock_Entrada), .K(1'b1), .Q(j_k_ff_1_q));  // open: Qn, preset, en, reset
  J_K_Flip_Flop j_k_ff_2 (.J(1'b1), .clk(j_k_ff_1_q), .K(1'b1), .Q(j_k_ff_2_q));  // open: Qn, preset, en, reset
  J_K_Flip_Flop j_k_ff_3 (.J(1'b1), .clk(j_k_ff_2_q), .K(1'b1), .Q(Clock_salida));  // open: Qn, preset, en, reset
endmodule

module SuperWorldPack (
  output [31:0] F0,
  output [31:0] F1,
  output [31:0] F2,
  output [31:0] F3,
  output [31:0] F4,
  output [31:0] F5,
  output [31:0] F6,
  output [31:0] F7,
  output [31:0] F8,
  output [31:0] F9,
  output [31:0] F10,
  output [31:0] F11,
  output [31:0] F12,
  output [31:0] F13,
  output [31:0] F14,
  output [31:0] F15,
  output [31:0] F16,
  output [31:0] F17,
  output [31:0] F18,
  output [31:0] F19,
  output [31:0] F20,
  output [31:0] F21,
  output [31:0] F22,
  output [31:0] F23,
  output [31:0] F24,
  output [31:0] F25,
  output [31:0] F26,
  output [31:0] F27,
  output [31:0] F28,
  output [31:0] F29,
  output [31:0] F30
);

  Comparator #(.width(32)) comparator_1 (.a(F0));  // open: b, gt, eq, lt
  Processor processor_1 (
    .F0(F0), .F1(F1), .F2(F2), .F3(F3), .F4(F4), .F5(F5), .F6(F6), .F7(F7), .F8(F8), .F9(F9), .F10(F10),
    .F11(F11), .F12(F12), .F13(F13), .F14(F14), .F15(F15), .F16(F16), .F17(F17), .F18(F18), .F19(F19),
    .F20(F20), .F21(F21), .F22(F22), .F23(F23), .F24(F24), .F25(F25), .F26(F26), .F27(F27), .F28(F28),
    .F29(F29), .F30(F30));  // open: L0, L1, L2
endmodule

module Processor (
  input  L0,
  input  L1,
  input  L2,
  output [31:0] F0,
  output [31:0] F1,
  output [31:0] F2,
  output [31:0] F3,
  output [31:0] F4,
  output [31:0] F5,
  output [31:0] F6,
  output [31:0] F7,
  output [31:0] F8,
  output [31:0] F9,
  output [31:0] F10,
  output [31:0] F11,
  output [31:0] F12,
  output [31:0] F13,
  output [31:0] F14,
  output [31:0] F15,
  output [31:0] F16,
  output [31:0] F17,
  output [31:0] F18,
  output [31:0] F19,
  output [31:0] F20,
  output [31:0] F21,
  output [31:0] F22,
  output [31:0] F23,
  output [31:0] F24,
  output [31:0] F25,
  output [31:0] F26,
  output [31:0] F27,
  output [31:0] F28,
  output [31:0] F29,
  output [31:0] F30
);

  wire [31:0] worldprocess_1_f0, worldprocess_1_f1, worldprocess_1_f2, worldprocess_1_f3, worldprocess_1_f4,
       worldprocess_1_f5, worldprocess_1_f6, worldprocess_1_f7, worldprocess_1_f8, worldprocess_1_f9,
       worldprocess_1_f10, worldprocess_1_f11, worldprocess_1_f12, worldprocess_1_f13, worldprocess_1_f14,
       worldprocess_1_f15, worldprocess_1_f16, worldprocess_1_f17, worldprocess_1_f18, worldprocess_1_f19,
       worldprocess_1_f20, worldprocess_1_f21, worldprocess_1_f22, worldprocess_1_f23, worldprocess_1_f24,
       worldprocess_1_f25, worldprocess_1_f26, worldprocess_1_f27, worldprocess_1_f28, worldprocess_1_f29,
       worldprocess_1_f30, worldprocess_2_f0, worldprocess_2_f1, worldprocess_2_f2, worldprocess_2_f3,
       worldprocess_2_f4, worldprocess_2_f5, worldprocess_2_f6, worldprocess_2_f7, worldprocess_2_f8,
       worldprocess_2_f9, worldprocess_2_f10, worldprocess_2_f11, worldprocess_2_f12, worldprocess_2_f13,
       worldprocess_2_f14, worldprocess_2_f15, worldprocess_2_f16, worldprocess_2_f17, worldprocess_2_f18,
       worldprocess_2_f19, worldprocess_2_f20, worldprocess_2_f21, worldprocess_2_f22, worldprocess_2_f23,
       worldprocess_2_f24, worldprocess_2_f25, worldprocess_2_f26, worldprocess_2_f27, worldprocess_2_f28,
       worldprocess_2_f29, worldprocess_2_f30, worldprocess_3_f0, worldprocess_3_f1, worldprocess_3_f2,
       worldprocess_3_f3, worldprocess_3_f4, worldprocess_3_f5, worldprocess_3_f6, worldprocess_3_f7,
       worldprocess_3_f8, worldprocess_3_f9, worldprocess_3_f10, worldprocess_3_f11, worldprocess_3_f12,
       worldprocess_3_f13, worldprocess_3_f14, worldprocess_3_f15, worldprocess_3_f16, worldprocess_3_f17,
       worldprocess_3_f18, worldprocess_3_f19, worldprocess_3_f20, worldprocess_3_f21, worldprocess_3_f22,
       worldprocess_3_f23, worldprocess_3_f24, worldprocess_3_f25, worldprocess_3_f26, worldprocess_3_f27,
       worldprocess_3_f28, worldprocess_3_f29, worldprocess_3_f30;

  WorldProcess worldprocess_1 (
    .reloj(L1), .F0(worldprocess_1_f0), .F1(worldprocess_1_f1), .F2(worldprocess_1_f2),
    .F3(worldprocess_1_f3), .F4(worldprocess_1_f4), .F5(worldprocess_1_f5), .F6(worldprocess_1_f6),
    .F7(worldprocess_1_f7), .F8(worldprocess_1_f8), .F9(worldprocess_1_f9), .F10(worldprocess_1_f10),
    .F11(worldprocess_1_f11), .F12(worldprocess_1_f12), .F13(worldprocess_1_f13), .F14(worldprocess_1_f14),
    .F15(worldprocess_1_f15), .F16(worldprocess_1_f16), .F17(worldprocess_1_f17), .F18(worldprocess_1_f18),
    .F19(worldprocess_1_f19), .F20(worldprocess_1_f20), .F21(worldprocess_1_f21), .F22(worldprocess_1_f22),
    .F23(worldprocess_1_f23), .F24(worldprocess_1_f24), .F25(worldprocess_1_f25), .F26(worldprocess_1_f26),
    .F27(worldprocess_1_f27), .F28(worldprocess_1_f28), .F29(worldprocess_1_f29), .F30(worldprocess_1_f30));
  assign F0 = worldprocess_2_f0 | worldprocess_1_f0 | worldprocess_3_f0;  // OR_Gate f0, 32 bits wide
  WorldProcess worldprocess_2 (
    .reloj(L0), .F0(worldprocess_2_f0), .F1(worldprocess_2_f1), .F2(worldprocess_2_f2),
    .F3(worldprocess_2_f3), .F4(worldprocess_2_f4), .F5(worldprocess_2_f5), .F6(worldprocess_2_f6),
    .F7(worldprocess_2_f7), .F8(worldprocess_2_f8), .F9(worldprocess_2_f9), .F10(worldprocess_2_f10),
    .F11(worldprocess_2_f11), .F12(worldprocess_2_f12), .F13(worldprocess_2_f13), .F14(worldprocess_2_f14),
    .F15(worldprocess_2_f15), .F16(worldprocess_2_f16), .F17(worldprocess_2_f17), .F18(worldprocess_2_f18),
    .F19(worldprocess_2_f19), .F20(worldprocess_2_f20), .F21(worldprocess_2_f21), .F22(worldprocess_2_f22),
    .F23(worldprocess_2_f23), .F24(worldprocess_2_f24), .F25(worldprocess_2_f25), .F26(worldprocess_2_f26),
    .F27(worldprocess_2_f27), .F28(worldprocess_2_f28), .F29(worldprocess_2_f29), .F30(worldprocess_2_f30));
  assign F2 = worldprocess_2_f2 | worldprocess_1_f2 | worldprocess_3_f2;  // OR_Gate f2, 32 bits wide
  assign F1 = worldprocess_2_f1 | worldprocess_1_f1 | worldprocess_3_f1;  // OR_Gate f1, 32 bits wide
  assign F3 = worldprocess_2_f3 | worldprocess_1_f3 | worldprocess_3_f3;  // OR_Gate f3, 32 bits wide
  assign F4 = worldprocess_2_f4 | worldprocess_1_f4 | worldprocess_3_f4;  // OR_Gate f4, 32 bits wide
  assign F6 = worldprocess_2_f6 | worldprocess_1_f6 | worldprocess_3_f6;  // OR_Gate f6, 32 bits wide
  assign F5 = worldprocess_2_f5 | worldprocess_1_f5 | worldprocess_3_f5;  // OR_Gate f5, 32 bits wide
  assign F8 = worldprocess_2_f8 | worldprocess_1_f8 | worldprocess_3_f8;  // OR_Gate f8, 32 bits wide
  assign F7 = worldprocess_2_f7 | worldprocess_1_f7 | worldprocess_3_f7;  // OR_Gate f7, 32 bits wide
  assign F9 = worldprocess_2_f9 | worldprocess_1_f9 | worldprocess_3_f9;  // OR_Gate f9, 32 bits wide
  assign F10 = worldprocess_2_f10 | worldprocess_1_f10 | worldprocess_3_f10;  // OR_Gate f10, 32 bits wide
  assign F12 = worldprocess_2_f12 | worldprocess_1_f12 | worldprocess_3_f12;  // OR_Gate f12, 32 bits wide
  assign F11 = worldprocess_2_f11 | worldprocess_1_f11 | worldprocess_3_f11;  // OR_Gate f11, 32 bits wide
  assign F13 = worldprocess_2_f13 | worldprocess_1_f13 | worldprocess_3_f13;  // OR_Gate f13, 32 bits wide
  assign F14 = worldprocess_2_f14 | worldprocess_1_f14 | worldprocess_3_f14;  // OR_Gate f14, 32 bits wide
  assign F16 = worldprocess_2_f16 | worldprocess_1_f16 | worldprocess_3_f16;  // OR_Gate f16, 32 bits wide
  assign F15 = worldprocess_2_f15 | worldprocess_1_f15 | worldprocess_3_f15;  // OR_Gate f15, 32 bits wide
  assign F17 = worldprocess_2_f17 | worldprocess_1_f17 | worldprocess_3_f17;  // OR_Gate f17, 32 bits wide
  assign F18 = worldprocess_2_f18 | worldprocess_1_f18 | worldprocess_3_f18;  // OR_Gate f18, 32 bits wide
  assign F19 = worldprocess_2_f19 | worldprocess_1_f19 | worldprocess_3_f19;  // OR_Gate f19, 32 bits wide
  assign F20 = worldprocess_2_f20 | worldprocess_1_f20 | worldprocess_3_f20;  // OR_Gate f20, 32 bits wide
  assign F21 = worldprocess_2_f21 | worldprocess_1_f21 | worldprocess_3_f21;  // OR_Gate f21, 32 bits wide
  assign F22 = worldprocess_2_f22 | worldprocess_1_f22 | worldprocess_3_f22;  // OR_Gate f22, 32 bits wide
  assign F24 = worldprocess_2_f24 | worldprocess_1_f24 | worldprocess_3_f24;  // OR_Gate f24, 32 bits wide
  assign F23 = worldprocess_2_f23 | worldprocess_1_f23 | worldprocess_3_f23;  // OR_Gate f23, 32 bits wide
  assign F26 = worldprocess_2_f26 | worldprocess_1_f26 | worldprocess_3_f26;  // OR_Gate f26, 32 bits wide
  assign F25 = worldprocess_2_f25 | worldprocess_1_f25 | worldprocess_3_f25;  // OR_Gate f25, 32 bits wide
  assign F27 = worldprocess_2_f27 | worldprocess_1_f27 | worldprocess_3_f27;  // OR_Gate f27, 32 bits wide
  assign F28 = worldprocess_2_f28 | worldprocess_1_f28 | worldprocess_3_f28;  // OR_Gate f28, 32 bits wide
  assign F30 = worldprocess_2_f30 | worldprocess_1_f30 | worldprocess_3_f30;  // OR_Gate f30, 32 bits wide
  assign F29 = worldprocess_2_f29 | worldprocess_1_f29 | worldprocess_3_f29;  // OR_Gate f29, 32 bits wide
  WorldProcess worldprocess_3 (
    .reloj(L2), .F0(worldprocess_3_f0), .F1(worldprocess_3_f1), .F2(worldprocess_3_f2),
    .F3(worldprocess_3_f3), .F4(worldprocess_3_f4), .F5(worldprocess_3_f5), .F6(worldprocess_3_f6),
    .F7(worldprocess_3_f7), .F8(worldprocess_3_f8), .F9(worldprocess_3_f9), .F10(worldprocess_3_f10),
    .F11(worldprocess_3_f11), .F12(worldprocess_3_f12), .F13(worldprocess_3_f13), .F14(worldprocess_3_f14),
    .F15(worldprocess_3_f15), .F16(worldprocess_3_f16), .F17(worldprocess_3_f17), .F18(worldprocess_3_f18),
    .F19(worldprocess_3_f19), .F20(worldprocess_3_f20), .F21(worldprocess_3_f21), .F22(worldprocess_3_f22),
    .F23(worldprocess_3_f23), .F24(worldprocess_3_f24), .F25(worldprocess_3_f25), .F26(worldprocess_3_f26),
    .F27(worldprocess_3_f27), .F28(worldprocess_3_f28), .F29(worldprocess_3_f29), .F30(worldprocess_3_f30));
endmodule
